# Fritzing sketch thermo_guide (saved by Fritzing 0.9.6b)
breadboards: 1

parts:
  Mod1 = Raspberry Pi 4B
  Part1 = Adafruit AMG8833 [part_number="Adafruit #3538"]
  Part2 = Logic Level Converter
  J1 = Basic Servo
  J2 = Basic Servo
  R1 = Resistor [tolerance=±5% resistance=4700 package="1206 [SMD]"]
  R2 = Resistor [tolerance=±5% resistance=4700 package="1206 [SMD]"]

nets:
  3V3: Mod1.3V3, Part1.VCC, Part1.3.3V, Part2.LV, R1.Pin_1, R2.Pin_0
  VCC: Mod1.5V, Part2.HV, J1.vcc, J2.vcc
  N1: Mod1.GPIO2, Part1.SDA, R2.Pin_1
  N2: Mod1.GPIO3, Part1.SCL, R1.Pin_0
  GND: Mod1.GND, Part1.GND, Part2.GND, J1.gnd, J2.gnd
  N3: Mod1.GPIO12, Part2.TX_LV
  N4: Mod1.GPIO13, Part2.TX2_LV
  N5: Part2.TX_HV, J2.pulse
  N6: Part2.TX2_HV, J1.pulse

custom parts:
  Adafruit AMG8833: Add heat-vision to your project and with an Adafruit AMG8833 Grid-EYE Breakout! This sensor from Panasonic is an 8x8 array of IR thermal sensors. When connected to your microcontroller (or raspberry Pi) it will return an array of 64 individual infrared temperature readings over I2C. It's like those fancy thermal cameras, but compact and simple enough for easy integration. This part will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
